# Fritzing sketch T-Display_MCP2515-CAN (saved by Fritzing 1.0.6)
breadboards: 1

parts:
  Mod1 = ESP32-TTGO-T-DISPLAY
  M1 = Niren can bus module [package=THT]
  A1 = XY-3606
  R2 = Resistor [tolerance=±5% power=0.25W resistance=2.2k package=THT]
  R3 = Resistor [tolerance=±5% power=0.25W resistance=3.3k package=THT]

nets:
  N1: Mod1.G-1, Mod1.G-2, Mod1.G-10, Mod1.G-11, Mod1.G-14, M1.pin2, A1.Pin_2, A1.Pin_3, R2.Pin_0
  N2: Mod1.5V, M1.pin1, A1.Pin_4
  N3: Mod1.26, M1.pin3
  N4: Mod1.25, M1.pin5
  N5: Mod1.33, M1.pin6
  N6: Mod1.32, R2.Pin_1, R3.Pin_0
  N7: M1.pin4, R3.Pin_1

notes:
  5V
  GND
  Harness GND
  Harness 12V
  XY-3606 Buck Step Down
  GPIO0 - Active/Listen Button
  GPIO35 - Display Wake/Sleep Button
  Power Options (Pick one):
  1. Buck Step Down to T-Display 5V Pins (Shown)
  2. Buck Step Down to T-Display USB-C (Pink)
  3. Center Console USB to T-Display USB-C (Purple)
  CAN H+ (Usually Pin 13)
  CAN L- (Usually Pin 14)
  3.3kΩ
  2.2kΩ
  Voltage Divider is highly recommended to step down the MCP2515 5V to ESP32 safe 3V

custom parts:
  ESP32-TTGO-T-DISPLAY: LILYGO TTGO T-Display GD32VF103CBT6 Main Chip ST7789 1.14 Inch IPS 240x135 Resolution Minimalist Development Board.
  Niren can bus module: Niren can bus module availabe on ebay and others. Pcb view assumes that you unsolder the 7 pin header and resolder it on the bottom of the module to connect to the pcb. The two jumpers and the can bus connector remain on the top of the board and don't appear in pcb view.
  XY-3606: 24V/12V turn 5V 5A power module, DC-DC XY-3606 Power Converter Super LM2596S.
